// Logisim project memory_game_final.circ as structural Verilog: 15 circuits, main circuit main
module main (
);

  wire b0, b1, b2, b3, b4, b5, b6, b7, b8, b9, b10, b11, b12, b13, Check, comparator_1_eq, comparator_1_gt,
       comparator_1_lt, correct, ep, game_end, help_btn, lose, miss, Mode, ModeButton, not_1_out, Play,
       Reset, SoundButton, SoundsON, TimeOut, win;
  wire [3:0] m0, m1, points, points1, points2, points22, points23, s0, s1, subtractor_1_out,
       subtractor_2_out, tries;
  wire [4:0] single_display_1_out_8, single_display_1_out_9, single_display_1_out_10,
       single_display_1_out_11, single_display_1_out_12, single_display_2_out_8, single_display_2_out_9,
       single_display_2_out_10, single_display_2_out_11, single_display_2_out_12, single_display_3_out_8,
       single_display_3_out_9, single_display_3_out_10, single_display_3_out_11, single_display_3_out_12,
       single_display_4_out_8, single_display_4_out_9, single_display_4_out_10, single_display_4_out_11,
       single_display_4_out_12, single_display_5_out_8, single_display_5_out_9, single_display_5_out_10,
       single_display_5_out_11, single_display_5_out_12, single_display_6_out_8, single_display_6_out_9,
       single_display_6_out_10, single_display_6_out_11, single_display_6_out_12, single_display_7_out_8,
       single_display_7_out_9, single_display_7_out_10, single_display_7_out_11, single_display_7_out_12,
       single_display_mirrored_1_out_8, single_display_mirrored_1_out_9, single_display_mirrored_1_out_10,
       single_display_mirrored_1_out_11, single_display_mirrored_1_out_12, single_display_mirrored_2_out_8,
       single_display_mirrored_2_out_9, single_display_mirrored_2_out_10, single_display_mirrored_2_out_11,
       single_display_mirrored_2_out_12, single_display_mirrored_3_out_8, single_display_mirrored_3_out_9,
       single_display_mirrored_3_out_10, single_display_mirrored_3_out_11, single_display_mirrored_3_out_12,
       single_display_mirrored_4_out_8, single_display_mirrored_4_out_9, single_display_mirrored_4_out_10,
       single_display_mirrored_4_out_11, single_display_mirrored_4_out_12, single_display_mirrored_5_out_8,
       single_display_mirrored_5_out_9, single_display_mirrored_5_out_10, single_display_mirrored_5_out_11,
       single_display_mirrored_5_out_12, single_display_mirrored_6_out_8, single_display_mirrored_6_out_9,
       single_display_mirrored_6_out_10, single_display_mirrored_6_out_11, single_display_mirrored_6_out_12,
       single_display_mirrored_7_out_8, single_display_mirrored_7_out_9, single_display_mirrored_7_out_10,
       single_display_mirrored_7_out_11, single_display_mirrored_7_out_12;
  wire [24:0] d0, d1, d2, d3, d4, d5, d6, d7, d8, d9, d10, d11, d12, d13;

  DotMatrix #(.matrixrows(1)) dotmatrix_1 ();  // open: col0, col1, col2, col3, col4
  Button button_1 (.out(Reset));
  Button button_2 (.out(Play));
  Button button_3 (.out(SoundButton));
  LED led_1 (.in(SoundsON));
  Button button_4 (.out(ModeButton));
  Button button_5 (.out(help_btn));
  LED led_2 (.in(Mode));
  not not_1 (not_1_out, Mode);
  LED led_3 (.in(not_1_out));
  Hex_Digit_Display hex_digit_display_1 (.value(tries));  // open: dp
  DotMatrix #(.matrixrows(5)) dotmatrix_2 (
    .col0(single_display_1_out_12), .col1(single_display_1_out_11), .col2(single_display_1_out_10),
    .col3(single_display_1_out_9), .col4(single_display_1_out_8));
  DotMatrix #(.matrixrows(5)) dotmatrix_3 (
    .col0(single_display_mirrored_1_out_8), .col1(single_display_mirrored_1_out_9),
    .col2(single_display_mirrored_1_out_10), .col3(single_display_mirrored_1_out_11),
    .col4(single_display_mirrored_1_out_12));
  single_display_mirrored single_display_mirrored_1 (
    .help_active(help_btn), .D(d1), .B(b1), .EP(ep), .MIS(miss), .correct(correct), .RES(Reset),
    .out_8(single_display_mirrored_1_out_8), .out_9(single_display_mirrored_1_out_9),
    .out_10(single_display_mirrored_1_out_10), .out_11(single_display_mirrored_1_out_11),
    .out_12(single_display_mirrored_1_out_12));
  Button button_6 (.out(Check));
  Hex_Digit_Display hex_digit_display_2 (.value(points2));  // open: dp
  single_display single_display_1 (
    .help(help_btn), .d(d0), .b(b0), .ep(ep), .miss(miss), .correct(correct), .in_7(Reset),
    .out_8(single_display_1_out_8), .out_9(single_display_1_out_9), .out_10(single_display_1_out_10),
    .out_11(single_display_1_out_11), .out_12(single_display_1_out_12));
  DotMatrix #(.matrixrows(5)) dotmatrix_4 (
    .col0(single_display_2_out_12), .col1(single_display_2_out_11), .col2(single_display_2_out_10),
    .col3(single_display_2_out_9), .col4(single_display_2_out_8));
  DotMatrix #(.matrixrows(5)) dotmatrix_5 (
    .col0(single_display_mirrored_2_out_8), .col1(single_display_mirrored_2_out_9),
    .col2(single_display_mirrored_2_out_10), .col3(single_display_mirrored_2_out_11),
    .col4(single_display_mirrored_2_out_12));
  single_display_mirrored single_display_mirrored_2 (
    .help_active(help_btn), .D(d3), .B(b3), .EP(ep), .MIS(miss), .correct(correct), .RES(Reset),
    .out_8(single_display_mirrored_2_out_8), .out_9(single_display_mirrored_2_out_9),
    .out_10(single_display_mirrored_2_out_10), .out_11(single_display_mirrored_2_out_11),
    .out_12(single_display_mirrored_2_out_12));
  Button button_7 (.out(b0));
  Button button_8 (.out(b1));
  T_Flip_Flop t_ff_1 (.T(SoundButton), .clk(SoundButton), .Qn(SoundsON));  // open: Q, reset, preset
  T_Flip_Flop t_ff_2 (.T(ModeButton), .clk(ModeButton), .Qn(Mode));  // open: Q, reset, preset
  HelpSystem helpsystem_1 (.help_btn(help_btn), .reset(Reset));  // open: help_active, buttons_disable
  Hex_Digit_Display hex_digit_display_3 (.value(points));  // open: dp
  single_display single_display_2 (
    .help(help_btn), .d(d2), .b(b2), .ep(ep), .miss(miss), .correct(correct), .in_7(Reset),
    .out_8(single_display_2_out_8), .out_9(single_display_2_out_9), .out_10(single_display_2_out_10),
    .out_11(single_display_2_out_11), .out_12(single_display_2_out_12));
  DotMatrix #(.matrixrows(5)) dotmatrix_6 (
    .col0(single_display_3_out_12), .col1(single_display_3_out_11), .col2(single_display_3_out_10),
    .col3(single_display_3_out_9), .col4(single_display_3_out_8));
  DotMatrix #(.matrixrows(5)) dotmatrix_7 (
    .col0(single_display_mirrored_3_out_8), .col1(single_display_mirrored_3_out_9),
    .col2(single_display_mirrored_3_out_10), .col3(single_display_mirrored_3_out_11),
    .col4(single_display_mirrored_3_out_12));
  single_display_mirrored single_display_mirrored_3 (
    .help_active(help_btn), .D(d5), .B(b5), .EP(ep), .MIS(miss), .correct(correct), .RES(Reset),
    .out_8(single_display_mirrored_3_out_8), .out_9(single_display_mirrored_3_out_9),
    .out_10(single_display_mirrored_3_out_10), .out_11(single_display_mirrored_3_out_11),
    .out_12(single_display_mirrored_3_out_12));
  Button button_9 (.out(b2));
  Button button_10 (.out(b4));
  Button button_11 (.out(b3));
  Button button_12 (.out(b5));
  single_display single_display_3 (
    .help(help_btn), .d(d4), .b(b4), .ep(ep), .miss(miss), .correct(correct), .in_7(Reset),
    .out_8(single_display_3_out_8), .out_9(single_display_3_out_9), .out_10(single_display_3_out_10),
    .out_11(single_display_3_out_11), .out_12(single_display_3_out_12));
  single_display single_display_4 (
    .help(help_btn), .d(d6), .b(b6), .ep(ep), .miss(miss), .correct(correct), .in_7(Reset),
    .out_8(single_display_4_out_8), .out_9(single_display_4_out_9), .out_10(single_display_4_out_10),
    .out_11(single_display_4_out_11), .out_12(single_display_4_out_12));
  DotMatrix #(.matrixrows(5)) dotmatrix_8 (
    .col0(single_display_4_out_12), .col1(single_display_4_out_11), .col2(single_display_4_out_10),
    .col3(single_display_4_out_9), .col4(single_display_4_out_8));
  DotMatrix #(.matrixrows(5)) dotmatrix_9 (
    .col0(single_display_mirrored_4_out_8), .col1(single_display_mirrored_4_out_9),
    .col2(single_display_mirrored_4_out_10), .col3(single_display_mirrored_4_out_11),
    .col4(single_display_mirrored_4_out_12));
  single_display_mirrored single_display_mirrored_4 (
    .help_active(help_btn), .D(d7), .B(b7), .EP(ep), .MIS(miss), .correct(correct), .RES(Reset),
    .out_8(single_display_mirrored_4_out_8), .out_9(single_display_mirrored_4_out_9),
    .out_10(single_display_mirrored_4_out_10), .out_11(single_display_mirrored_4_out_11),
    .out_12(single_display_mirrored_4_out_12));
  Button button_13 (.out(b6));
  Button button_14 (.out(b8));
  Button button_15 (.out(b7));
  Button button_16 (.out(b9));
  Hex_Digit_Display hex_digit_display_4 (.value(m1));  // open: dp
  Hex_Digit_Display hex_digit_display_5 (.value(m0));  // open: dp
  single_display single_display_5 (
    .help(help_btn), .d(d8), .b(b8), .ep(ep), .miss(miss), .correct(correct), .in_7(Reset),
    .out_8(single_display_5_out_8), .out_9(single_display_5_out_9), .out_10(single_display_5_out_10),
    .out_11(single_display_5_out_11), .out_12(single_display_5_out_12));
  DotMatrix #(.matrixrows(5)) dotmatrix_10 (
    .col0(single_display_5_out_12), .col1(single_display_5_out_11), .col2(single_display_5_out_10),
    .col3(single_display_5_out_9), .col4(single_display_5_out_8));
  DotMatrix #(.matrixrows(5)) dotmatrix_11 (
    .col0(single_display_mirrored_5_out_8), .col1(single_display_mirrored_5_out_9),
    .col2(single_display_mirrored_5_out_10), .col3(single_display_mirrored_5_out_11),
    .col4(single_display_mirrored_5_out_12));
  single_display_mirrored single_display_mirrored_5 (
    .help_active(help_btn), .D(d9), .B(b9), .EP(ep), .MIS(miss), .correct(correct), .RES(Reset),
    .out_8(single_display_mirrored_5_out_8), .out_9(single_display_mirrored_5_out_9),
    .out_10(single_display_mirrored_5_out_10), .out_11(single_display_mirrored_5_out_11),
    .out_12(single_display_mirrored_5_out_12));
  Button button_17 (.out(b10));
  Button button_18 (.out(b12));
  Button button_19 (.out(b11));
  Button button_20 (.out(b13));
  DotMatrix #(.matrixcols(1), .matrixrows(1)) dotmatrix_12 ();  // open: col0
  DotMatrix #(.matrixcols(1), .matrixrows(1)) dotmatrix_13 ();  // open: col0
  Hex_Digit_Display hex_digit_display_6 (.value(s1));  // open: dp
  single_display single_display_6 (
    .help(help_btn), .d(d10), .b(b10), .ep(ep), .miss(miss), .correct(correct), .in_7(Reset),
    .out_8(single_display_6_out_8), .out_9(single_display_6_out_9), .out_10(single_display_6_out_10),
    .out_11(single_display_6_out_11), .out_12(single_display_6_out_12));
  DotMatrix #(.matrixrows(5)) dotmatrix_14 (
    .col0(single_display_6_out_12), .col1(single_display_6_out_11), .col2(single_display_6_out_10),
    .col3(single_display_6_out_9), .col4(single_display_6_out_8));
  DotMatrix #(.matrixrows(5)) dotmatrix_15 (
    .col0(single_display_mirrored_6_out_8), .col1(single_display_mirrored_6_out_9),
    .col2(single_display_mirrored_6_out_10), .col3(single_display_mirrored_6_out_11),
    .col4(single_display_mirrored_6_out_12));
  single_display_mirrored single_display_mirrored_6 (
    .help_active(help_btn), .D(d11), .B(b11), .EP(ep), .MIS(miss), .correct(correct), .RES(Reset),
    .out_8(single_display_mirrored_6_out_8), .out_9(single_display_mirrored_6_out_9),
    .out_10(single_display_mirrored_6_out_10), .out_11(single_display_mirrored_6_out_11),
    .out_12(single_display_mirrored_6_out_12));
  Hex_Digit_Display hex_digit_display_7 (.value(s0));  // open: dp
  single_display single_display_7 (
    .help(help_btn), .d(d12), .b(b12), .ep(ep), .miss(miss), .correct(correct), .in_7(Reset),
    .out_8(single_display_7_out_8), .out_9(single_display_7_out_9), .out_10(single_display_7_out_10),
    .out_11(single_display_7_out_11), .out_12(single_display_7_out_12));
  DotMatrix #(.matrixrows(5)) dotmatrix_16 (
    .col0(single_display_7_out_12), .col1(single_display_7_out_11), .col2(single_display_7_out_10),
    .col3(single_display_7_out_9), .col4(single_display_7_out_8));
  DotMatrix #(.matrixrows(5)) dotmatrix_17 (
    .col0(single_display_mirrored_7_out_8), .col1(single_display_mirrored_7_out_9),
    .col2(single_display_mirrored_7_out_10), .col3(single_display_mirrored_7_out_11),
    .col4(single_display_mirrored_7_out_12));
  single_display_mirrored single_display_mirrored_7 (
    .help_active(help_btn), .D(d13), .B(b13), .EP(ep), .MIS(miss), .correct(correct), .RES(Reset),
    .out_8(single_display_mirrored_7_out_8), .out_9(single_display_mirrored_7_out_9),
    .out_10(single_display_mirrored_7_out_10), .out_11(single_display_mirrored_7_out_11),
    .out_12(single_display_mirrored_7_out_12));
  LED led_4 (.in(win));
  LED led_5 (.in(lose));
  SoundSystem soundsystem_1 (.Reset(Reset), .SoundsON(SoundsON), .Match(correct), .Wrong(miss), .Win(win), .Lose(lose));
  Clock clock_1 ();  // open: out
  buttons buttons_1 (
    .check(Check), .b0(b0), .b1(b1), .b2(b2), .b3(b3), .b4(b4), .b5(b5), .b6(b6), .b7(b7), .b8(b8), .b9(b9),
    .b10(b10), .b11(b11), .b12(b12), .b13(b13), .d0(d0), .d1(d1), .d2(d2), .d3(d3), .d4(d4), .d5(d5),
    .d6(d6), .d7(d7), .d8(d8), .d9(d9), .d10(d10), .d11(d11), .d12(d12), .d13(d13), .correct(correct),
    .wrong(miss));
  screen screen_1 (
    .in_1(Play), .in_2(Reset), .win(win), .lose(lose), .d0(d0), .d1(d1), .d2(d2), .d3(d3), .d4(d4), .d5(d5),
    .d6(d6), .d7(d7), .d8(d8), .d9(d9), .d10(d10), .d11(d11), .d12(d12), .d13(d13), .placing_done(ep));
  timer timer_1 (.set(Play), .reset(Reset), .game_end(game_end), .TimeOut(TimeOut), .t3(m1), .t2(m0), .t1(s1), .t0(s0));
  score score_1 (
    .timeOut(TimeOut), .mode(Mode), .correct(correct), .wrong(miss), .reset(Reset), .win(win),
    .points(points1), .lose(lose), .tries(tries));
  or or_1 (game_end, win, lose);
  // Probe on points1
  Comparator #(.mode("unsigned"), .width(4)) comparator_1 (
    .a(points1), .b(4'b1001), .gt(comparator_1_gt), .eq(comparator_1_eq), .lt(comparator_1_lt));
  Multiplexer #(.width(4)) multiplexer_1 (.in0(4'b0000), .in1(4'b0001), .out(points22), .sel(comparator_1_eq));
  Multiplexer #(.width(4)) multiplexer_2 (.in0(4'b0000), .in1(4'b0001), .out(points23), .sel(comparator_1_gt));
  Subtractor #(.width(4)) subtractor_1 (.a(points1), .b(4'b1001), .out(subtractor_1_out));  // open: bin, bout
  Subtractor #(.width(4)) subtractor_2 (.a(subtractor_1_out), .b(4'b0001), .out(subtractor_2_out));  // open: bin, bout
  Multiplexer #(.width(4)) multiplexer_3 (.in0(points23), .in1(points22), .out(points2), .sel(comparator_1_eq));
  // Probe on points
  Multiplexer #(.width(4)) multiplexer_4 (.in0(points1), .in1(subtractor_2_out), .out(points), .sel(comparator_1_gt));
  // Probe on points2

  // Notes on the sheet:
  //   HardMode
  //   EasyMode
endmodule

module screen (
  input  in_1,
  input  in_2,
  input  win,
  input  lose,
  output [24:0] d0,
  output [24:0] d1,
  output [24:0] d2,
  output [24:0] d3,
  output [24:0] d4,
  output [24:0] d5,
  output [24:0] d6,
  output [24:0] d7,
  output [24:0] d8,
  output [24:0] d9,
  output [24:0] d10,
  output [24:0] d11,
  output [24:0] d12,
  output [24:0] d13,
  output placing_done
);

  wire and_1_out, and_3_out, and_4_out, and_5_out, and_6_out, and_7_out, and_8_out, and_9_out, and_11_out,
       and_12_out, and_13_out, and_14_out, and_15_out, and_16_out, and_17_out, clk, doCount, end_b, eq0, eq1,
       eq2, eq3, eq4, eq5, eq6, eq7, eq8, eq9, eq10, eq11, eq12, eq13, game_end, n0, n1, n2, n3, n4, n5, n6,
       n7, n8, n9, n10, n11, n12, n13, not_1_out, not_2_out, not_3_out, not_4_out, not_5_out, not_6_out,
       not_7_out, not_8_out, not_9_out, not_10_out, not_11_out, not_12_out, not_13_out, not_14_out,
       not_15_out, not_16_out, or_2_out, r0, r1, r2, r3, r4, r5, r6, r7, r8, r9, r10, r11, r12, r13, start;
  wire [1:0] priority_encoder_1_out, priority_encoder_2_out, priority_encoder_3_out, priority_encoder_4_out,
       priority_encoder_5_out, priority_encoder_6_out, priority_encoder_7_out, priority_encoder_8_out,
       priority_encoder_9_out, priority_encoder_10_out, priority_encoder_11_out, priority_encoder_12_out,
       priority_encoder_13_out, priority_encoder_14_out;
  wire [3:0] count, randN;
  wire [24:0] c0, c1, c2, c3, c4, c5, c6, d0_t, d1_t, d2_t, d3_t, d4_t, d5_t, d6_t, d7_t, d8_t, d9_t, d10_t,
       d11_t, d12_t, d13_t, multiplexer_1_out, multiplexer_2_out, multiplexer_3_out, multiplexer_4_out,
       multiplexer_5_out, multiplexer_6_out, multiplexer_7_out, multiplexer_8_out, multiplexer_9_out,
       multiplexer_10_out, multiplexer_11_out, multiplexer_12_out, multiplexer_13_out, multiplexer_14_out,
       multiplexer_15_out;

  Clock clock_1 (.out(clk));
  deck deck_1 (.in_1(in_1), .in_2(in_2), .c6(c6), .c4(c4), .c0(c0), .c2(c2), .c5(c5), .c1(c1), .c3(c3), .out_10(end_b));
  not not_1 (not_1_out, game_end);
  not not_2 (not_2_out, game_end);
  not not_3 (not_3_out, game_end);
  not not_4 (not_4_out, game_end);
  not not_5 (not_5_out, game_end);
  not not_6 (not_6_out, game_end);
  Priority_Encoder #(.select(2)) priority_encoder_1 (
    .in0(not_6_out), .in1(win), .in2(lose), .out(priority_encoder_1_out));  // open: in3, gs, en_out, en_in
  not not_7 (not_7_out, game_end);
  Priority_Encoder #(.select(2)) priority_encoder_2 (
    .in0(not_7_out), .in1(win), .in2(lose), .out(priority_encoder_2_out));  // open: in3, gs, en_out, en_in
  Multiplexer #(.select(4), .width(25)) multiplexer_1 (
    .in0(c0), .in1(c0), .in2(c1), .in3(c1), .in4(c2), .in5(c2), .in6(c3), .in7(c3), .in8(c4), .in9(c4),
    .in10(c5), .in11(c5), .in12(c6), .in13(c6), .out(multiplexer_1_out), .sel(count));  // open: in14, in15
  Priority_Encoder #(.select(2)) priority_encoder_3 (
    .in0(not_1_out), .in1(win), .in2(lose), .out(priority_encoder_3_out));  // open: in3, gs, en_out, en_in
  Priority_Encoder #(.select(2)) priority_encoder_4 (
    .in0(not_2_out), .in1(win), .in2(lose), .out(priority_encoder_4_out));  // open: in3, gs, en_out, en_in
  Priority_Encoder #(.select(2)) priority_encoder_5 (
    .in0(not_3_out), .in1(win), .in2(lose), .out(priority_encoder_5_out));  // open: in3, gs, en_out, en_in
  Priority_Encoder #(.select(2)) priority_encoder_6 (
    .in0(not_4_out), .in1(win), .in2(lose), .out(priority_encoder_6_out));  // open: in3, gs, en_out, en_in
  Priority_Encoder #(.select(2)) priority_encoder_7 (
    .in0(not_5_out), .in1(win), .in2(lose), .out(priority_encoder_7_out));  // open: in3, gs, en_out, en_in
  Multiplexer #(.select(2), .width(25)) multiplexer_2 (
    .in0(d10_t), .in1({25{1'b0}}), .in2({25{1'b0}}), .out(multiplexer_2_out), .sel(priority_encoder_1_out));  // open: in3
  Multiplexer #(.select(2), .width(25)) multiplexer_3 (
    .in0(d12_t), .in1({25{1'b0}}), .in2(25'hfd6b5), .out(multiplexer_3_out), .sel(priority_encoder_2_out));  // open: in3
  Demultiplexer #(.select(4), .width(25)) demultiplexer_1 (
    .out0(d0_t), .out1(d1_t), .out2(d2_t), .out3(d3_t), .out4(d4_t), .out5(d5_t), .out6(d6_t), .out7(d7_t),
    .out8(d8_t), .out9(d9_t), .out10(d10_t), .out11(d11_t), .out12(d12_t), .out13(d13_t),
    .in(multiplexer_1_out), .sel(randN));  // open: out14, out15
  Multiplexer #(.select(2), .width(25)) multiplexer_4 (
    .in0(d0_t), .in1({25{1'b0}}), .in2(25'h1f8d6e0), .out(multiplexer_4_out), .sel(priority_encoder_3_out));  // open: in3
  Multiplexer #(.select(2), .width(25)) multiplexer_5 (
    .in0(d2_t), .in1(25'h1041d10), .in2({25{1'b0}}), .out(multiplexer_5_out), .sel(priority_encoder_4_out));  // open: in3
  Multiplexer #(.select(2), .width(25)) multiplexer_6 (
    .in0(d4_t), .in1(25'h1f8c7e0), .in2(25'h1fa53e0), .out(multiplexer_6_out), .sel(priority_encoder_5_out));  // open: in3
  Multiplexer #(.select(2), .width(25)) multiplexer_7 (
    .in0(d6_t), .in1(25'hf843f), .in2({25{1'b0}}), .out(multiplexer_7_out), .sel(priority_encoder_6_out));  // open: in3
  Multiplexer #(.select(2), .width(25)) multiplexer_8 (
    .in0(d8_t), .in1({25{1'b0}}), .in2(25'h1f4111f), .out(multiplexer_8_out), .sel(priority_encoder_7_out));  // open: in3
  Register #(.width(25)) register_1 (.D(multiplexer_2_out), .en(r10), .clk(clk), .Q(d10), .clr(in_2));
  Register #(.width(25)) register_2 (.D(multiplexer_3_out), .en(r12), .clk(clk), .Q(d12), .clr(in_2));
  and and_1 (and_1_out, start, not_8_out);
  not not_8 (not_8_out, game_end);
  Register #(.width(25)) register_3 (.D(multiplexer_4_out), .en(r0), .clk(clk), .Q(d0), .clr(in_2));
  Register #(.width(25)) register_4 (.D(multiplexer_5_out), .en(r2), .clk(clk), .Q(d2), .clr(in_2));
  Register #(.width(25)) register_5 (.D(multiplexer_6_out), .en(r4), .clk(clk), .Q(d4), .clr(in_2));
  Register #(.width(25)) register_6 (.D(multiplexer_7_out), .en(r6), .clk(clk), .Q(d6), .clr(in_2));
  Register #(.width(25)) register_7 (.D(multiplexer_8_out), .en(r8), .clk(clk), .Q(d8), .clr(in_2));
  Random #(.width(4)) random_1 (.next(and_1_out), .clk(clk), .out(randN));  // open: clr
  // Probe on randN
  or or_1 (game_end, win, lose);
  not not_9 (not_9_out, game_end);
  not not_10 (not_10_out, game_end);
  not not_11 (not_11_out, game_end);
  not not_12 (not_12_out, game_end);
  not not_13 (not_13_out, game_end);
  not not_14 (not_14_out, game_end);
  not not_15 (not_15_out, game_end);
  Priority_Encoder #(.select(2)) priority_encoder_8 (
    .in0(not_9_out), .in1(win), .in2(lose), .out(priority_encoder_8_out));  // open: in3, gs, en_out, en_in
  Priority_Encoder #(.select(2)) priority_encoder_9 (
    .in0(not_10_out), .in1(win), .in2(lose), .out(priority_encoder_9_out));  // open: in3, gs, en_out, en_in
  Priority_Encoder #(.select(2)) priority_encoder_10 (
    .in0(not_11_out), .in1(win), .in2(lose), .out(priority_encoder_10_out));  // open: in3, gs, en_out, en_in
  Priority_Encoder #(.select(2)) priority_encoder_11 (
    .in0(not_12_out), .in1(win), .in2(lose), .out(priority_encoder_11_out));  // open: in3, gs, en_out, en_in
  Priority_Encoder #(.select(2)) priority_encoder_12 (
    .in0(not_13_out), .in1(win), .in2(lose), .out(priority_encoder_12_out));  // open: in3, gs, en_out, en_in
  Priority_Encoder #(.select(2)) priority_encoder_13 (
    .in0(not_14_out), .in1(win), .in2(lose), .out(priority_encoder_13_out));  // open: in3, gs, en_out, en_in
  Priority_Encoder #(.select(2)) priority_encoder_14 (
    .in0(not_15_out), .in1(win), .in2(lose), .out(priority_encoder_14_out));  // open: in3, gs, en_out, en_in
  Counter #(.max('he), .width(4)) counter_1 (
    .clr(not_16_out), .count(doCount), .clk(clk), .Q(count));  // open: load, up, D, carry
  not not_16 (not_16_out, end_b);
  Register #(.width(25)) register_8 (.D(multiplexer_9_out), .en(r1), .clk(clk), .Q(d1), .clr(in_2));
  Multiplexer #(.select(2), .width(25)) multiplexer_9 (
    .in0(d1_t), .in1({25{1'b0}}), .in2(25'h1f8c7e0), .out(multiplexer_9_out), .sel(priority_encoder_8_out));  // open: in3
  Register #(.width(25)) register_9 (.D(multiplexer_10_out), .en(r3), .clk(clk), .Q(d3), .clr(in_2));
  Multiplexer #(.select(2), .width(25)) multiplexer_10 (
    .in0(d3_t), .in1(25'h1e1907e), .in2({25{1'b0}}), .out(multiplexer_10_out), .sel(priority_encoder_9_out));  // open: in3
  Register #(.width(25)) register_10 (.D(multiplexer_11_out), .en(r5), .clk(clk), .Q(d5), .clr(in_2));
  Multiplexer #(.select(2), .width(25)) multiplexer_11 (
    .in0(d5_t), .in1(25'h8fe20), .in2(25'h18304d8), .out(multiplexer_11_out), .sel(priority_encoder_10_out));  // open: in3
  Register #(.width(25)) register_11 (.D(multiplexer_12_out), .en(r7), .clk(clk), .Q(d7), .clr(in_2));
  Multiplexer #(.select(2), .width(25)) multiplexer_12 (
    .in0(d7_t), .in1(25'h1f4105f), .in2({25{1'b0}}), .out(multiplexer_12_out), .sel(priority_encoder_11_out));  // open: in3
  Register #(.width(25)) register_12 (.D(multiplexer_13_out), .en(r9), .clk(clk), .Q(d9), .clr(in_2));
  Multiplexer #(.select(2), .width(25)) multiplexer_13 (
    .in0(d9_t), .in1({25{1'b0}}), .in2(25'hfd6b5), .out(multiplexer_13_out), .sel(priority_encoder_12_out));  // open: in3
  Multiplexer #(.select(2), .width(25)) multiplexer_14 (
    .in0(d11_t), .in1({25{1'b0}}), .in2({25{1'b0}}), .out(multiplexer_14_out), .sel(priority_encoder_13_out));  // open: in3
  Multiplexer #(.select(2), .width(25)) multiplexer_15 (
    .in0(d13_t), .in1({25{1'b0}}), .in2(25'hfd28b), .out(multiplexer_15_out), .sel(priority_encoder_14_out));  // open: in3
  Register #(.width(25)) register_13 (.D(multiplexer_14_out), .en(r11), .clk(clk), .Q(d11), .clr(in_2));
  Register #(.width(25)) register_14 (.D(multiplexer_15_out), .en(r13), .clk(clk), .Q(d13), .clr(in_2));
  or or_2 (or_2_out, eq10, eq11, eq0, eq1, eq2, eq3, eq4, eq5, eq6, eq7, eq8, eq9, eq12, eq13);
  Comparator #(.width(25)) comparator_1 (.a(d0), .b({25{1'b0}}), .eq(eq0));  // open: gt, lt
  Comparator #(.width(25)) comparator_2 (.a(d2), .b({25{1'b0}}), .eq(eq2));  // open: gt, lt
  Comparator #(.width(25)) comparator_3 (.a(d4), .b({25{1'b0}}), .eq(eq4));  // open: gt, lt
  Comparator #(.width(25)) comparator_4 (.a(d6), .b({25{1'b0}}), .eq(eq6));  // open: gt, lt
  Comparator #(.width(25)) comparator_5 (.a(d8), .b({25{1'b0}}), .eq(eq8));  // open: gt, lt
  Comparator #(.width(25)) comparator_6 (.a(d10), .b({25{1'b0}}), .eq(eq10));  // open: gt, lt
  Comparator #(.width(25)) comparator_7 (.a(d12), .b({25{1'b0}}), .eq(eq12));  // open: gt, lt
  and and_2 (start, or_2_out, end_b);
  and and_3 (and_3_out, n0, eq0);
  and and_4 (and_4_out, n2, eq2);
  and and_5 (and_5_out, n4, eq4);
  and and_6 (and_6_out, n6, eq6);
  and and_7 (and_7_out, n8, eq8);
  and and_8 (and_8_out, n10, eq10);
  and and_9 (and_9_out, n12, eq12);
  or or_3 (r0, game_end, and_3_out);
  or or_4 (r2, game_end, and_4_out);
  or or_5 (r4, game_end, and_5_out);
  or or_6 (r6, game_end, and_6_out);
  or or_7 (r8, game_end, and_7_out);
  or or_8 (r10, game_end, and_8_out);
  or or_9 (r12, game_end, and_9_out);
  Multiplexer #(.select(4)) multiplexer_16 (
    .in0(r0), .in1(r1), .in2(r2), .in3(r3), .in4(r4), .in5(r5), .in6(r6), .in7(r7), .in8(r8), .in9(r9),
    .in10(r10), .in11(r11), .in12(r12), .in13(r13), .in14(1'b0), .in15(1'b0), .out(doCount), .sel(randN));
  and and_10 (placing_done, ~eq11, ~eq10, ~eq0, ~eq1, ~eq2, ~eq3, ~eq4, ~eq5, ~eq6, ~eq7, ~eq8, ~eq9, ~eq12, ~eq13);  // AND_Gate
  Demultiplexer #(.select(4)) demultiplexer_2 (
    .out0(n0), .out1(n1), .out2(n2), .out3(n3), .out4(n4), .out5(n5), .out6(n6), .out7(n7), .out8(n8),
    .out9(n9), .out10(n10), .out11(n11), .out12(n12), .out13(n13), .in(start), .sel(randN));  // open: out14, out15
  Comparator #(.width(25)) comparator_8 (.a(d1), .b({25{1'b0}}), .eq(eq1));  // open: gt, lt
  Comparator #(.width(25)) comparator_9 (.a(d3), .b({25{1'b0}}), .eq(eq3));  // open: gt, lt
  Comparator #(.width(25)) comparator_10 (.a(d5), .b({25{1'b0}}), .eq(eq5));  // open: gt, lt
  Comparator #(.width(25)) comparator_11 (.a(d7), .b({25{1'b0}}), .eq(eq7));  // open: gt, lt
  Comparator #(.width(25)) comparator_12 (.a(d9), .b({25{1'b0}}), .eq(eq9));  // open: gt, lt
  Comparator #(.width(25)) comparator_13 (.a(d11), .b({25{1'b0}}), .eq(eq11));  // open: gt, lt
  Comparator #(.width(25)) comparator_14 (.a(d13), .b({25{1'b0}}), .eq(eq13));  // open: gt, lt
  and and_11 (and_11_out, n1, eq1);
  and and_12 (and_12_out, n3, eq3);
  and and_13 (and_13_out, n5, eq5);
  and and_14 (and_14_out, n7, eq7);
  and and_15 (and_15_out, n9, eq9);
  and and_16 (and_16_out, n11, eq11);
  and and_17 (and_17_out, n13, eq13);
  or or_10 (r1, game_end, and_11_out);
  or or_11 (r3, game_end, and_12_out);
  or or_12 (r5, game_end, and_13_out);
  or or_13 (r7, game_end, and_14_out);
  or or_14 (r9, game_end, and_15_out);
  or or_15 (r11, game_end, and_16_out);
  or or_16 (r13, game_end, and_17_out);

  // Other names for the same wires on the sheet: q0[24:0] = d0; q1[24:0] = d1; q2[24:0] = d2; q3[24:0] = d3;
  //   q4[24:0] = d4; q5[24:0] = d5; q6[24:0] = d6; q7[24:0] = d7; q8[24:0] = d8; q9[24:0] = d9; q10[24:0] = d10;
  //   q11[24:0] = d11; q12[24:0] = d12; q13[24:0] = d13; reset = in_2; set = in_1
endmodule

module deck (
  input  in_1,
  input  in_2,
  output [24:0] c6,
  output [24:0] c4,
  output [24:0] c0,
  output [24:0] c2,
  output [24:0] c5,
  output [24:0] c1,
  output [24:0] c3,
  output out_10
);

  wire clk, not_1_out, r0, r1, r2, r3, r4, r5, r6, s_r_ff_1_q, start;
  wire [2:0] count;
  wire [4:0] bit_extender_1_out, bit_extender_2_out, bit_extender_3_out, bit_extender_4_out,
       bit_extender_5_out, bit_extender_6_out, bit_extender_7_out, bit_extender_8_out, bit_extender_9_out,
       bit_extender_10_out, bit_extender_11_out, bit_extender_12_out, bit_extender_13_out,
       bit_extender_14_out, bit_extender_15_out, bit_extender_16_out, bit_extender_17_out,
       bit_extender_18_out, bit_extender_19_out, bit_extender_20_out, bit_extender_21_out;
  wire [8:0] c0_t, c1_t, c2_t, c3_t, c4_t, c5_t, c6_t, random_1_out, register_1_q, register_2_q,
       register_3_q, register_4_q, register_5_q, register_6_q, register_7_q;

  Clock clock_1 (.out(clk));
  Random #(.width(9)) random_1 (.next(not_1_out), .clk(clk), .out(random_1_out));  // open: clr
  not not_1 (not_1_out, out_10);
  Register #(.width(9)) register_1 (.D(c0_t), .en(r0), .clk(clk), .Q(register_1_q), .clr(in_2));
  Register #(.width(9)) register_2 (.D(c1_t), .en(r1), .clk(clk), .Q(register_2_q), .clr(in_2));
  Demultiplexer #(.select(3), .width(9)) demultiplexer_1 (
    .out0(c0_t), .out1(c1_t), .out2(c2_t), .out3(c3_t), .out4(c4_t), .out5(c5_t), .out6(c6_t),
    .in(random_1_out), .sel(count));  // open: out7
  assign bit_extender_1_out = {{2{1'b0}}, register_1_q[2:0]};  // Bit_Extender bit_extender_1
  assign bit_extender_2_out = {{2{1'b0}}, register_1_q[5:3]};  // Bit_Extender bit_extender_2
  assign bit_extender_3_out = {{2{1'b0}}, register_1_q[8:6]};  // Bit_Extender bit_extender_3
  assign bit_extender_4_out = {{2{1'b0}}, register_2_q[2:0]};  // Bit_Extender bit_extender_4
  assign bit_extender_5_out = {{2{1'b0}}, register_2_q[5:3]};  // Bit_Extender bit_extender_5
  assign bit_extender_6_out = {{2{1'b0}}, register_2_q[8:6]};  // Bit_Extender bit_extender_6
  Shifter #(.width(5)) shifter_1 (.in(bit_extender_1_out), .\dist (3'b001), .out(c0[9:5]));
  Shifter #(.width(5)) shifter_2 (.in(bit_extender_2_out), .\dist (3'b001), .out(c0[14:10]));
  Shifter #(.width(5)) shifter_3 (.in(bit_extender_3_out), .\dist (3'b001), .out(c0[19:15]));
  Shifter #(.width(5)) shifter_4 (.in(bit_extender_4_out), .\dist (3'b001), .out(c1[9:5]));
  Shifter #(.width(5)) shifter_5 (.in(bit_extender_5_out), .\dist (3'b001), .out(c1[14:10]));
  Shifter #(.width(5)) shifter_6 (.in(bit_extender_6_out), .\dist (3'b001), .out(c1[19:15]));
  Register #(.width(9)) register_3 (.D(c2_t), .en(r2), .clk(clk), .Q(register_3_q), .clr(in_2));
  Register #(.width(9)) register_4 (.D(c3_t), .en(r3), .clk(clk), .Q(register_4_q), .clr(in_2));
  Counter #(.max('h7), .width(3)) counter_1 (
    .clr(in_2), .count(start), .clk(clk), .carry(out_10), .Q(count));  // open: load, up, D
  assign bit_extender_7_out = {{2{1'b0}}, register_3_q[2:0]};  // Bit_Extender bit_extender_7
  Shifter #(.width(5)) shifter_7 (.in(bit_extender_7_out), .\dist (3'b001), .out(c2[9:5]));
  assign bit_extender_8_out = {{2{1'b0}}, register_3_q[5:3]};  // Bit_Extender bit_extender_8
  Shifter #(.width(5)) shifter_8 (.in(bit_extender_8_out), .\dist (3'b001), .out(c2[14:10]));
  assign bit_extender_9_out = {{2{1'b0}}, register_3_q[8:6]};  // Bit_Extender bit_extender_9
  Shifter #(.width(5)) shifter_9 (.in(bit_extender_9_out), .\dist (3'b001), .out(c2[19:15]));
  assign bit_extender_10_out = {{2{1'b0}}, register_4_q[2:0]};  // Bit_Extender bit_extender_10
  Shifter #(.width(5)) shifter_10 (.in(bit_extender_10_out), .\dist (3'b001), .out(c3[9:5]));
  assign bit_extender_11_out = {{2{1'b0}}, register_4_q[5:3]};  // Bit_Extender bit_extender_11
  Shifter #(.width(5)) shifter_11 (.in(bit_extender_11_out), .\dist (3'b001), .out(c3[14:10]));
  assign bit_extender_12_out = {{2{1'b0}}, register_4_q[8:6]};  // Bit_Extender bit_extender_12
  Shifter #(.width(5)) shifter_12 (.in(bit_extender_12_out), .\dist (3'b001), .out(c3[19:15]));
  Decoder #(.select(3)) decoder_1 (
    .out0(r0), .out1(r1), .out2(r2), .out3(r3), .out4(r4), .out5(r5), .out6(r6), .sel(count));  // open: out7, en
  Register #(.width(9)) register_5 (.D(c4_t), .en(r4), .clk(clk), .Q(register_5_q), .clr(in_2));
  Register #(.width(9)) register_6 (.D(c5_t), .en(r5), .clk(clk), .Q(register_6_q), .clr(in_2));
  assign bit_extender_13_out = {{2{1'b0}}, register_5_q[2:0]};  // Bit_Extender bit_extender_13
  Shifter #(.width(5)) shifter_13 (.in(bit_extender_13_out), .\dist (3'b001), .out(c4[9:5]));
  assign bit_extender_14_out = {{2{1'b0}}, register_5_q[5:3]};  // Bit_Extender bit_extender_14
  Shifter #(.width(5)) shifter_14 (.in(bit_extender_14_out), .\dist (3'b001), .out(c4[14:10]));
  assign bit_extender_15_out = {{2{1'b0}}, register_5_q[8:6]};  // Bit_Extender bit_extender_15
  Shifter #(.width(5)) shifter_15 (.in(bit_extender_15_out), .\dist (3'b001), .out(c4[19:15]));
  assign bit_extender_16_out = {{2{1'b0}}, register_6_q[2:0]};  // Bit_Extender bit_extender_16
  Shifter #(.width(5)) shifter_16 (.in(bit_extender_16_out), .\dist (3'b001), .out(c5[9:5]));
  assign bit_extender_17_out = {{2{1'b0}}, register_6_q[5:3]};  // Bit_Extender bit_extender_17
  Shifter #(.width(5)) shifter_17 (.in(bit_extender_17_out), .\dist (3'b001), .out(c5[14:10]));
  assign bit_extender_18_out = {{2{1'b0}}, register_6_q[8:6]};  // Bit_Extender bit_extender_18
  Shifter #(.width(5)) shifter_18 (.in(bit_extender_18_out), .\dist (3'b001), .out(c5[19:15]));
  S_R_Flip_Flop s_r_ff_1 (.S(in_1), .R(in_2), .clk(clk), .Q(s_r_ff_1_q));  // open: reset, Qn, preset
  and and_1 (start, s_r_ff_1_q, ~out_10);  // AND_Gate
  Register #(.width(9)) register_7 (.D(c6_t), .en(r6), .clk(clk), .Q(register_7_q), .clr(in_2));
  assign bit_extender_19_out = {{2{1'b0}}, register_7_q[2:0]};  // Bit_Extender bit_extender_19
  assign bit_extender_20_out = {{2{1'b0}}, register_7_q[5:3]};  // Bit_Extender bit_extender_20
  assign bit_extender_21_out = {{2{1'b0}}, register_7_q[8:6]};  // Bit_Extender bit_extender_21
  Shifter #(.width(5)) shifter_19 (.in(bit_extender_19_out), .\dist (3'b001), .out(c6[9:5]));
  Shifter #(.width(5)) shifter_20 (.in(bit_extender_20_out), .\dist (3'b001), .out(c6[14:10]));
  Shifter #(.width(5)) shifter_21 (.in(bit_extender_21_out), .\dist (3'b001), .out(c6[19:15]));

  assign {c0[24:20], c0[4:0]} = {10{1'b0}};
  assign {c1[24:20], c1[4:0]} = {10{1'b0}};
  assign {c2[24:20], c2[4:0]} = {10{1'b0}};
  assign {c3[24:20], c3[4:0]} = {10{1'b0}};
  assign {c4[24:20], c4[4:0]} = {10{1'b0}};
  assign {c5[24:20], c5[4:0]} = {10{1'b0}};
  assign {c6[24:20], c6[4:0]} = {10{1'b0}};

  // Other names for the same wires on the sheet: reset = in_2; set = in_1; stop = out_10
endmodule

// sc
module score (
  input  timeOut,
  input  mode,
  input  correct,
  input  wrong,
  input  reset,
  output win,
  output [3:0] points,
  output lose,
  output [3:0] tries
);

  wire and_2_out, and_3_out, bonus, clock_1_out, clock_2_out, clock_3_out, correct_pulse, counter_2_carry,
       d_ff_1_q, mistake_pulse, not_1_out, not_2_out, or_1_out, prev_correct_q, WE;
  wire [2:0] streak_data, streak_next, streak_plus1, streak_q;
  wire [3:0] adder_1_out, matches_q, multiplexer_1_out, multiplexer_4_out, new_points;

  // AND_Gate and_1 has open pins: in0=correct, in1=wrong, out=open
  and and_2 (and_2_out, wrong, ~correct);  // AND_Gate
  Multiplexer #(.width(4)) multiplexer_1 (.in0(4'b0100), .in1(4'b0010), .out(multiplexer_1_out), .sel(mode));
  Counter #(.max('hf), .ongoal("stay"), .width(4)) counter_1 (
    .clr(reset), .load(correct_pulse), .count(1'b1), .clk(correct_pulse), .D(new_points), .Q(points));  // open: up, carry
  Counter #(.max('h4), .ongoal("stay"), .width(4)) counter_2 (
    .load(reset), .up(1'b0), .clk(or_1_out), .D(multiplexer_1_out), .carry(counter_2_carry), .Q(tries));  // open: clr, count
  or or_1 (or_1_out, reset, and_2_out);
  Clock #(.highDuration(3), .lowDuration(3)) clock_1 (.out(clock_1_out));
  Clock #(.highDuration(3), .lowDuration(3)) clock_2 (.out(clock_2_out));
  D_Flip_Flop d_ff_1 (.D(wrong), .clk(clock_2_out), .Q(d_ff_1_q), .reset(reset));  // open: Qn, preset
  Clock #(.highDuration(3), .lowDuration(3)) clock_3 (.out(clock_3_out));
  D_Flip_Flop prev_correct (.D(correct), .clk(clock_1_out), .Q(prev_correct_q), .reset(reset));  // open: Qn, preset
  Register #(.width(3)) streak (.D(streak_data), .en(WE), .clk(clock_3_out), .Q(streak_q), .clr(reset));
  and and_3 (and_3_out, timeOut, mode);
  Multiplexer #(.width(3)) multiplexer_2 (.in0(3'b000), .in1(streak_plus1), .out(streak_data), .sel(correct_pulse));
  Multiplexer #(.width(3)) multiplexer_3 (.in0(streak_data), .in1(3'b000), .out(streak_next), .sel(mistake_pulse));
  Counter #(.max('hf), .width(4)) \matches  (
    .clr(reset), .clk(correct_pulse), .Q(matches_q));  // open: load, up, count, D, carry
  Adder #(.width(4)) adder_1 (.a(points), .b(4'b0001), .out(adder_1_out));  // open: cin, cout
  or or_2 (lose, and_3_out, counter_2_carry);
  not not_1 (not_1_out, prev_correct_q);
  not not_2 (not_2_out, d_ff_1_q);
  Adder #(.width(3)) adder_2 (.a(streak_q), .b(3'b001), .out(streak_plus1));  // open: cin, cout
  Adder #(.width(4)) adder_3 (.a(adder_1_out), .b(multiplexer_4_out), .out(new_points));  // open: cin, cout
  Multiplexer #(.width(4)) multiplexer_4 (.in0(4'b0000), .in1(4'b0001), .out(multiplexer_4_out), .sel(bonus));
  and and_4 (correct_pulse, not_1_out, correct);
  and and_5 (mistake_pulse, not_2_out, wrong);
  or or_3 (bonus, streak_q[0], streak_q[1], streak_q[2]);
  or or_4 (WE, mistake_pulse, correct_pulse);
  Comparator #(.width(4)) comparator_1 (.a(matches_q), .b(4'b0111), .eq(win));  // open: gt, lt
endmodule

module timer (
  input  set,
  input  reset,
  input  game_end,
  output TimeOut,
  output [3:0] t3,
  output [3:0] t2,
  output [3:0] t1,
  output [3:0] t0
);

  wire a_min, a_sec, h, min, or_1_out, or_2_out, or_3_out;

  or or_1 (or_1_out, min, reset);
  or or_2 (or_2_out, h, reset);
  seconds_counter seconds_counter_1 (.game_end(game_end), .reset(reset), .set(set), .asec(a_sec), .s(t0));
  Counter #(.max('h5), .width(4)) counter_1 (
    .clr(or_1_out), .clk(a_sec), .carry(min), .Q(t1));  // open: load, up, count, D
  Counter #(.max('h9), .width(4)) counter_2 (
    .clr(or_2_out), .clk(a_min), .carry(h), .Q(t3));  // open: load, up, count, D
  or or_3 (or_3_out, a_min, reset);
  Counter #(.max('h9), .width(4)) counter_3 (
    .clr(or_3_out), .clk(min), .carry(a_min), .Q(t2));  // open: load, up, count, D
  Comparator #(.width(4)) comparator_1 (.a(t2), .b(4'b0011), .eq(TimeOut));  // open: gt, lt

  // Notes on the sheet:
  //   3 min
endmodule

// s
module seconds_counter (
  input  game_end,
  input  reset,
  input  set,
  output asec,
  output [3:0] s
);

  wire clk, hz64, or_1_out, or_2_out, s_r_ff_1_q, start;

  Clock clock_1 (.out(clk));
  or or_1 (or_1_out, asec, reset);
  Counter #(.max('hb), .width(4)) counter_1 (
    .clr(or_2_out), .count(start), .clk(clk), .carry(hz64));  // open: load, up, D, Q
  or or_2 (or_2_out, hz64, reset);
  Counter #(.max('h9), .width(4)) counter_2 (
    .clr(or_1_out), .clk(hz64), .carry(asec), .Q(s));  // open: load, up, count, D
  S_R_Flip_Flop s_r_ff_1 (.S(set), .R(reset), .clk(clk), .Q(s_r_ff_1_q));  // open: reset, Qn, preset
  and and_1 (start, ~game_end, s_r_ff_1_q);  // AND_Gate
endmodule

module buttons (
  input  check,
  input  b0,
  input  b1,
  input  b2,
  input  b3,
  input  b4,
  input  b5,
  input  b6,
  input  b7,
  input  b8,
  input  b9,
  input  b10,
  input  b11,
  input  b12,
  input  b13,
  input  [24:0] d0,
  input  [24:0] d1,
  input  [24:0] d2,
  input  [24:0] d3,
  input  [24:0] d4,
  input  [24:0] d5,
  input  [24:0] d6,
  input  [24:0] d7,
  input  [24:0] d8,
  input  [24:0] d9,
  input  [24:0] d10,
  input  [24:0] d11,
  input  [24:0] d12,
  input  [24:0] d13,
  output correct,
  output wrong
);

  wire bcheck, bx, c0, c1, clk, comparator_1_eq, reset, stop;
  wire [3:0] b_sel;
  wire [24:0] dx, register_1_q, register_2_q;

  Clock clock_1 (.out(clk));
  Priority_Encoder #(.select(4)) priority_encoder_1 (
    .in0(b0), .in1(b1), .in2(b2), .in3(b3), .in4(b4), .in5(b5), .in6(b6), .in7(b7), .in8(b8), .in9(b9),
    .in10(b10), .in11(b11), .in12(b12), .in13(b13), .out(b_sel));  // open: in14, in15, gs, en_out, en_in
  Counter #(.max('h3), .width(2)) counter_1 (
    .clr(reset), .clk(bcheck), .carry(stop), .Q({c1, c0}));  // open: load, up, count, D
  Multiplexer #(.select(4), .width(25)) multiplexer_1 (
    .in0(d0), .in1(d1), .in2(d2), .in3(d3), .in4(d4), .in5(d5), .in6(d6), .in7(d7), .in8(d8), .in9(d9),
    .in10(d10), .in11(d11), .in12(d12), .in13(d13), .out(dx), .sel(b_sel));  // open: in14, in15
  ExactlyOne xor_1 (
    .out(bx), .in0(b10), .in1(b11), .in2(b0), .in3(b1), .in4(b2), .in5(b3), .in6(b4), .in7(b5), .in8(b6),
    .in9(b7), .in10(b8), .in11(b9), .in12(b12), .in13(b13));
  Register #(.trigger("falling"), .width(25)) register_1 (.D(dx), .en(c0), .clk(bx), .Q(register_1_q));  // open: clr
  Register #(.trigger("falling"), .width(25)) register_2 (.D(dx), .en(c1), .clk(bx), .Q(register_2_q));  // open: clr
  Counter #(.max('h1), .width(1)) counter_2 (
    .clr(reset), .count(stop), .clk(clk), .carry(reset));  // open: load, up, D, Q
  Comparator #(.width(25)) comparator_1 (.a(register_1_q), .b(register_2_q), .eq(comparator_1_eq));  // open: gt, lt
  and and_1 (correct, comparator_1_eq, stop);
  and and_2 (wrong, ~correct, stop);  // AND_Gate
  ExactlyOne xor_2 (
    .out(bcheck), .in0(b11), .in1(b10), .in2(b0), .in3(b1), .in4(b2), .in5(b3), .in6(b4), .in7(b5), .in8(b6),
    .in9(b7), .in10(b8), .in11(b9), .in12(b12), .in13(b13), .in14(check));
endmodule

// _
module single_display (
  input  help,
  input  [24:0] d,
  input  b,
  input  ep,
  input  miss,
  input  correct,
  input  in_7,
  output [4:0] out_8,
  output [4:0] out_9,
  output [4:0] out_10,
  output [4:0] out_11,
  output [4:0] out_12
);

  wire and_1_out, and_2_out, clk, comparator_1_eq, dis, help_active, multiplexer_2_out, not_1_out, or_1_out,
       or_2_out, s_r_ff_2_q, s_r_ff_3_q, stop;
  wire [3:0] timer_1_t0;

  timer timer_1 (.set(ep), .reset(stop), .t0(timer_1_t0));  // open: game_end, TimeOut, t3, t2, t1
  Comparator #(.width(4)) comparator_1 (.a(timer_1_t0), .b(4'b0011), .eq(comparator_1_eq));  // open: gt, lt
  S_R_Flip_Flop s_r_ff_1 (.S(comparator_1_eq), .R(not_1_out), .clk(clk), .Q(stop));  // open: reset, Qn, preset
  not not_1 (not_1_out, ep);
  S_R_Flip_Flop s_r_ff_2 (.Q(s_r_ff_2_q), .reset(or_2_out), .preset(b));  // open: S, R, clk, Qn
  Multiplexer #(.width(25)) multiplexer_1 (
    .in0(d), .in1({25{1'b0}}), .out({out_12, out_11, out_10, out_9, out_8}), .sel(multiplexer_2_out));
  and and_1 (and_1_out, stop, ~or_1_out);  // AND_Gate
  or or_1 (or_1_out, s_r_ff_2_q, s_r_ff_3_q);
  or or_2 (or_2_out, miss, in_7);
  S_R_Flip_Flop s_r_ff_3 (.Q(s_r_ff_3_q), .reset(in_7), .preset(and_2_out));  // open: S, R, clk, Qn
  and and_2 (and_2_out, s_r_ff_2_q, correct);
  Multiplexer multiplexer_2 (.in0(and_1_out), .in1(1'b0), .out(multiplexer_2_out), .sel(help_active));
  Clock clock_1 (.out(clk));
  HelpSystem helpsystem_1 (.help_btn(help), .reset(in_7), .help_active(help_active), .buttons_disable(dis));

  // Other names for the same wires on the sheet: b_press = b; dx[24:0] = d; mistake = miss; reset = in_7
endmodule

// __
module single_display_mirrored (
  input  help_active,
  input  [24:0] D,
  input  B,
  input  EP,
  input  MIS,
  input  correct,
  input  RES,
  output [4:0] out_8,
  output [4:0] out_9,
  output [4:0] out_10,
  output [4:0] out_11,
  output [4:0] out_12
);

  wire and_1_out, and_2_out, clk, comparator_1_eq, dis, help_active_t, multiplexer_2_out, not_1_out,
       or_1_out, or_2_out, s_r_ff_2_q, s_r_ff_3_q, stop;
  wire [3:0] timer_1_t0;

  timer timer_1 (.set(EP), .reset(stop), .t0(timer_1_t0));  // open: game_end, TimeOut, t3, t2, t1
  Comparator #(.width(4)) comparator_1 (.a(timer_1_t0), .b(4'b0011), .eq(comparator_1_eq));  // open: gt, lt
  S_R_Flip_Flop s_r_ff_1 (.S(comparator_1_eq), .R(not_1_out), .clk(clk), .Q(stop));  // open: reset, Qn, preset
  not not_1 (not_1_out, EP);
  Multiplexer #(.width(25)) multiplexer_1 (
    .in0(D), .in1({25{1'b0}}), .out({out_8, out_9, out_10, out_11, out_12}), .sel(multiplexer_2_out));
  and and_1 (and_1_out, stop, ~or_1_out);  // AND_Gate
  or or_1 (or_1_out, s_r_ff_2_q, s_r_ff_3_q);
  S_R_Flip_Flop s_r_ff_2 (.Q(s_r_ff_2_q), .reset(or_2_out), .preset(B));  // open: S, R, clk, Qn
  or or_2 (or_2_out, MIS, RES);
  and and_2 (and_2_out, s_r_ff_2_q, correct);
  S_R_Flip_Flop s_r_ff_3 (.Q(s_r_ff_3_q), .reset(RES), .preset(and_2_out));  // open: S, R, clk, Qn
  Multiplexer multiplexer_2 (.in0(and_1_out), .in1(1'b0), .out(multiplexer_2_out), .sel(help_active_t));
  Clock clock_1 (.out(clk));
  HelpSystem helpsystem_1 (.help_btn(help_active), .reset(RES), .help_active(help_active_t), .buttons_disable(dis));

  // Other names for the same wires on the sheet: b_press = B; dx[24:0] = D; help = help_active; mistake = MIS;
  //   reset = RES
endmodule

module GameWon (
  input  Reset,
  input  GameWon
);

  wire clock_1_out, comparator_1_eq, comparator_1_lt, counter_1_carry, counter_2_carry, d_ff_1_q, or_1_out,
       or_2_out;
  wire [3:0] counter_2_q;
  wire [13:0] rom_1_data;

  Clock clock_1 (.out(clock_1_out));
  Counter #(.max('h7), .width(3)) counter_1 (
    .count(clock_1_out), .clk(clock_1_out), .carry(counter_1_carry));  // open: clr, load, up, D, Q
  D_Flip_Flop d_ff_1 (.D(GameWon), .clk(GameWon), .Q(d_ff_1_q), .reset(or_2_out));  // open: Qn, preset
  or or_1 (or_1_out, comparator_1_lt, d_ff_1_q);
  or or_2 (or_2_out, Reset, comparator_1_eq);
  Counter #(.max('hf), .width(4)) counter_2 (
    .clr(or_2_out), .count(or_1_out), .clk(counter_1_carry), .carry(counter_2_carry), .Q(counter_2_q));  // open: load, up, D
  ROM #(.addrWidth(4), .dataWidth(14)) rom_1 (.addr(counter_2_q), .data(rom_1_data));
  Comparator #(.width(14)) comparator_1 (
    .a(14'h1), .b(rom_1_data), .eq(comparator_1_eq), .lt(comparator_1_lt));  // open: gt
  // Buzzer #(.smooth_level(8), .smooth_width(8), .vol_width(8)) buzzer_1: pin names not known; wires that end beside it: rom_1_data, 8'h60, 1'b1

  // Notes on the sheet:
  //   contents of rom_1 (hex, n*v repeats v):
  //   0 190 190 200 190 190 200 200 258 258 190 258 3e8 3e8 4e8 1
endmodule

module GameLost (
  input  Reset,
  input  GameLost
);

  wire clock_1_out, comparator_1_eq, comparator_1_lt, counter_1_carry, counter_2_carry, d_ff_1_q, or_1_out,
       or_2_out;
  wire [3:0] counter_2_q;
  wire [13:0] rom_1_data;

  Clock clock_1 (.out(clock_1_out));
  Counter #(.max('h7), .width(3)) counter_1 (
    .count(clock_1_out), .clk(clock_1_out), .carry(counter_1_carry));  // open: clr, load, up, D, Q
  D_Flip_Flop d_ff_1 (.D(GameLost), .clk(GameLost), .Q(d_ff_1_q), .reset(or_2_out));  // open: Qn, preset
  or or_1 (or_1_out, comparator_1_lt, d_ff_1_q);
  or or_2 (or_2_out, Reset, comparator_1_eq);
  Counter #(.max('hf), .width(4)) counter_2 (
    .clr(or_2_out), .count(or_1_out), .clk(counter_1_carry), .carry(counter_2_carry), .Q(counter_2_q));  // open: load, up, D
  ROM #(.addrWidth(4), .dataWidth(14)) rom_1 (.addr(counter_2_q), .data(rom_1_data));
  Comparator #(.width(14)) comparator_1 (
    .a(14'h1), .b(rom_1_data), .eq(comparator_1_eq), .lt(comparator_1_lt));  // open: gt
  // Buzzer #(.smooth_level(8), .smooth_width(8), .vol_width(8)) buzzer_1: pin names not known; wires that end beside it: rom_1_data, 8'h60, 1'b1

  // Notes on the sheet:
  //   contents of rom_1 (hex, n*v repeats v):
  //   0 200 400 600 800 500 800 200 200 700 700 150 100 1
endmodule

module SoundSystem (
  input  Reset,
  input  SoundsON,
  input  Match,
  input  Wrong,
  input  Win,
  input  Lose
);

  wire and_1_out, and_2_out, and_3_out, and_4_out;

  and and_1 (and_1_out, SoundsON, Match);
  and and_2 (and_2_out, SoundsON, Wrong);
  and and_3 (and_3_out, SoundsON, Win);
  and and_4 (and_4_out, SoundsON, Lose);
  CorrectMatch correctmatch_1 (.Reset(Reset), .Match(and_1_out));
  WrongMatch wrongmatch_1 (.Reset(Reset), .Wrong(and_2_out));
  GameWon gamewon_1 (.Reset(Reset), .GameWon(and_3_out));
  GameLost gamelost_1 (.Reset(Reset), .GameLost(and_4_out));
endmodule

module CorrectMatch (
  input  Reset,
  input  Match
);

  wire clock_1_out, comparator_1_eq, comparator_1_lt, counter_1_carry, counter_2_carry, d_ff_1_q, or_1_out,
       or_2_out;
  wire [3:0] counter_2_q;
  wire [13:0] rom_1_data;

  Clock clock_1 (.out(clock_1_out));
  Counter #(.max('h7), .width(3)) counter_1 (
    .count(clock_1_out), .clk(clock_1_out), .carry(counter_1_carry));  // open: clr, load, up, D, Q
  D_Flip_Flop d_ff_1 (.D(Match), .clk(Match), .Q(d_ff_1_q), .reset(or_2_out));  // open: Qn, preset
  or or_1 (or_1_out, comparator_1_lt, d_ff_1_q);
  or or_2 (or_2_out, Reset, comparator_1_eq);
  Counter #(.max('hf), .width(4)) counter_2 (
    .clr(or_2_out), .count(or_1_out), .clk(counter_1_carry), .carry(counter_2_carry), .Q(counter_2_q));  // open: load, up, D
  ROM #(.addrWidth(4), .dataWidth(14)) rom_1 (.addr(counter_2_q), .data(rom_1_data));
  Comparator #(.width(14)) comparator_1 (
    .a(14'h1), .b(rom_1_data), .eq(comparator_1_eq), .lt(comparator_1_lt));  // open: gt
  // Buzzer #(.smooth_level(8), .smooth_width(8), .vol_width(8)) buzzer_1: pin names not known; wires that end beside it: rom_1_data, 8'h60, 1'b1

  // Notes on the sheet:
  //   contents of rom_1 (hex, n*v repeats v):
  //   0 400 350 1 5*0 100
endmodule

module WrongMatch (
  input  Reset,
  input  Wrong
);

  wire clock_1_out, comparator_1_eq, comparator_1_lt, counter_1_carry, counter_2_carry, d_ff_1_q, or_1_out,
       or_2_out;
  wire [3:0] counter_2_q;
  wire [13:0] rom_1_data;

  Clock clock_1 (.out(clock_1_out));
  Counter #(.max('h7), .width(3)) counter_1 (
    .count(clock_1_out), .clk(clock_1_out), .carry(counter_1_carry));  // open: clr, load, up, D, Q
  D_Flip_Flop d_ff_1 (.D(Wrong), .clk(Wrong), .Q(d_ff_1_q), .reset(or_2_out));  // open: Qn, preset
  or or_1 (or_1_out, comparator_1_lt, d_ff_1_q);
  or or_2 (or_2_out, Reset, comparator_1_eq);
  Counter #(.max('hf), .width(4)) counter_2 (
    .clr(or_2_out), .count(or_1_out), .clk(counter_1_carry), .carry(counter_2_carry), .Q(counter_2_q));  // open: load, up, D
  ROM #(.addrWidth(4), .dataWidth(14)) rom_1 (.addr(counter_2_q), .data(rom_1_data));
  Comparator #(.width(14)) comparator_1 (
    .a(14'h1), .b(rom_1_data), .eq(comparator_1_eq), .lt(comparator_1_lt));  // open: gt
  // Buzzer #(.smooth_level(8), .smooth_width(8), .vol_width(8)) buzzer_1: pin names not known; wires that end beside it: rom_1_data, 8'h60, 1'b1

  // Notes on the sheet:
  //   contents of rom_1 (hex, n*v repeats v):
  //   0 100 800 800 100 800 1 0 0 100
endmodule

module HelpSystem (
  input  help_btn,
  input  reset,
  output help_active,
  output buttons_disable
);

  wire active1, asec_help, button_1_out, clk, counter_3_carry, counter_reset, D, help_pulse, hz64, not_1_out,
       not_2_out, or_1_out, or_2_out, or_4_out, prev_help_q;
  wire [3:0] counter_1_q, undriven;

  Button button_1 (.out(button_1_out));
  Clock #(.highDuration(3), .lowDuration(3)) clock_1 (.out(clk));
  Register #(.width(1)) prev_help (.D(help_btn), .en(1'b1), .clk(clk), .Q(prev_help_q), .clr(reset));
  Register #(.width(1)) help_ff (.D(D), .en(1'b1), .clk(clk), .Q(help_active), .clr(reset));
  not not_1 (not_1_out, prev_help_q);
  or or_1 (or_1_out, active1, reset);
  Counter #(.max('h5), .ongoal("stay"), .width(4)) counter_1 (
    .clr(or_1_out), .count(help_active), .clk(hz64), .carry(active1), .Q(counter_1_q));  // open: load, up, D
  and and_1 (help_pulse, help_btn, not_1_out);
  and and_2 (asec_help, active1, help_active);
  or or_2 (or_2_out, help_active, help_pulse);
  not not_2 (not_2_out, buttons_disable);
  or or_3 (counter_reset, help_pulse, reset);
  and and_3 (D, or_2_out, not_2_out);
  Comparator #(.width(4)) comparator_1 (.a(counter_1_q), .b(4'b0010), .eq(buttons_disable));  // open: gt, lt
  Counter #(.max('hb), .width(4)) counter_2 (.clr(or_4_out), .clk(clk), .carry(hz64));  // open: load, up, count, D, Q
  or or_4 (or_4_out, hz64, reset);
  Counter #(.max('h2), .width(4)) counter_3 (
    .clr(reset), .clk(hz64), .carry(counter_3_carry));  // open: load, up, count, D, Q
  Comparator #(.width(4)) comparator_2 (.a(4'b1111), .b(undriven));  // open: gt, eq, lt

  // Other names for the same wires on the sheet: help_done = buttons_disable; stop = help_active
endmodule
